# Fritzing sketch diagramaesp32 (saved by Fritzing 1.0.8)
breadboards: 2

parts:
  M1 = DOIT Esp32 DevKit v1 (30 pins long, 11 pins width) [part_number=ESP32S-PIN30]
  R2 = Photocell (LDR) [power=0.25W dark_resistance_@0.01lx=300kΩ light_resistance_@100lx=400Ω luminance=10lx package=THT]
  R1 = Photocell (LDR) [power=0.25W dark_resistance_@0.01lx=300kΩ light_resistance_@100lx=400Ω luminance=10lx package=THT]
  R3 = Resistor [tolerance=±5% power=0.25W resistance=10k package=THT]
  R4 = Resistor [tolerance=±5% power=0.25W resistance=10k package=THT]
  OLED1 = SSD1306 0,96" OLED 128x64 I2C
  DHT3 = Humidity and Temperature Sensor DHT11
  DHT4 = Humidity and Temperature Sensor DHT11

nets:
  VCC: M1.3V3, R2.pin_1, R1.pin_1, OLED1.VDD, DHT3.Vcc, DHT4.Vcc
  GND: M1.GND, R3.Pin_0, R4.Pin_0, OLED1.GND, DHT3.GND_1, DHT4.GND_1
  N1: M1.D4, DHT3.Data-signal
  N2: M1.D5, DHT4.Data-signal
  N3: M1.D21, OLED1.SCK
  N4: M1.D22, OLED1.SDA
  N5: M1.D34, R1.pin_0, R3.Pin_1
  N6: M1.D35, R2.pin_0, R4.Pin_1

custom parts:
  DOIT Esp32 DevKit v1 (30 pins long, 11 pins width): The DOIT Esp32 DevKit v1 is one of the development board created by DOIT to evaluate the ESP-WROOM-32 module. It is based on the ESP32 microcontroller that boasts Wifi, Bluetooth, Ethernet and Low Power support all in a single chip. (vanepp) made breadboard work, adjusted pin numbering and labels and reduced size of schematic and cleaned up pcb. This chip is 30pins long (2 x15) and 11 pins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
  SSD1306 0,96" OLED 128x64 I2C: YUS
  Humidity and Temperature Sensor DHT11: Digital relative humidity & temperature sensor DHT11
